# Fritzing sketch Alarm Clock (saved by Fritzing 0.9.3b)
breadboards: 1

parts:
  MBED1 = mbed
  U1 = ESP8266 WiFi Module [part_number=ESP8266]
  R1 = Resistor [tolerance=±5% resistance=10k package="2010 [SMD]"]
  R2 = Resistor [tolerance=±5% resistance=10k package="2010 [SMD]"]
  U2 = LCD-16X2 [package=lcd-16x2]
  R3 = Resistor [tolerance=±5% resistance=220 package="2010 [SMD]"]
  R4 = Resistor [tolerance=±5% resistance=470 package="2010 [SMD]"]

nets:
  GND: MBED1.GND, U1.CH_PD, U1.GND
  N1: MBED1.pin14, U2.RS
  N2: MBED1.pin15, U2.E
  N3: MBED1.pin17, U2.DB4
  N4: MBED1.pin18, U2.DB5
  N5: MBED1.pin19, U2.DB6
  N6: MBED1.pin20, U2.DB7
  N7: MBED1.pin21, U2.R_W
  N8: MBED1.pin26, U1.RST
  N9: MBED1.pin27, U1.TXD
  N10: MBED1.pin28, U1.RXD
  N11: MBED1.VU, U2.VDD
  N12: MBED1.VOUT, U1.VCC
  N13: U1.GPIO_0, R1.Pin_0
  N14: U1.GPIO_2, R2.Pin_0
  N15: U2.VSS, U2.K
  N16: U2.VO, R4.Pin_0
  N17: U2.A, R3.Pin_0
  N18: R3.Pin_1, R4.Pin_1

custom parts:
  mbed: A powerful microcontroller board based on the NXP LPC processor with an ARM Cortex core. See http://mbed.org for more info.
  ESP8266 WiFi Module: Generic WiFi Module based on the ESP8266 with onboard PCB antenna and UART communications
